# Fritzing sketch Wiring (saved by Fritzing 0.9.3b)

parts:
  Part1 = Adafruit RFM69HCW Transceiver Radio [part_number="Adafruit #3070 and #3071"]
  Raspberry_Pi_1 = Raspberry Pi 3 [part_number=RPI-3-V1.2]

nets:
  VIN: Part1.VIN, Raspberry_Pi_1.GIPO27, Raspberry_Pi_1.3V3
  GND: Part1.GND, Raspberry_Pi_1.GND
  N1: Part1.EN, Part1.DIO0, Raspberry_Pi_1.GIPO24
  N2: Part1.SCK, Raspberry_Pi_1.GIPO11
  N3: Part1.MISO, Raspberry_Pi_1.GIPO9
  N4: Part1.MOSI, Raspberry_Pi_1.GIPO10
  N5: Part1.CS, Raspberry_Pi_1.GIPO8
  N6: Part1.RST, Raspberry_Pi_1.GIPO25

custom parts:
  Adafruit RFM69HCW Transceiver Radio: Sending data over long distances is like magic, and now you can be a magician with this range of powerful and easy-to-use radio modules. Sure, sometimes you want to talk to a computer (a good time to use WiFi) or perhaps communicate with a Phone (choose Bluetooth Low Energy!) but what if you want to send data very far? Most WiFi, Bluetooth, Zigbee and other wireless chipsets use 2.4GHz, which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
